// Logisim project ALU.circ as structural Verilog: 1 circuit, main circuit ALU
module ALU (
  input  [7:0] INP1,
  input  [7:0] INP2,
  input  [3:0] MUX_Con,
  output [7:0] OUT
);

  wire [7:0] adder_1_out, adder_2_out, AND_out, buffer_1_out, buffer_2_out, not_1_out, not_2_out, OR_out,
       subtractor_1_out, subtractor_2_out;

  Subtractor subtractor_1 (.a(INP1), .b(INP2), .out(subtractor_1_out));  // open: bin, bout
  Adder adder_1 (.a(INP1), .b(8'h1), .out(adder_1_out));  // open: cin, cout
  Subtractor subtractor_2 (.a(INP2), .b(8'h1), .out(subtractor_2_out));  // open: bin, bout
  Adder adder_2 (.a(INP1), .b(INP2), .out(adder_2_out));  // open: cin, cout
  assign AND_out = INP1 & INP2;  // AND_Gate AND, 8 bits wide
  assign OR_out = INP1 | INP2;  // OR_Gate OR, 8 bits wide
  assign not_1_out = ~INP1;  // NOT_Gate not_1, 8 bits wide
  assign not_2_out = ~INP2;  // NOT_Gate not_2, 8 bits wide
  assign buffer_1_out = INP1;  // Buffer buffer_1, 8 bits wide
  assign buffer_2_out = INP2;  // Buffer buffer_2, 8 bits wide
  Multiplexer #(.select(4), .width(8)) multiplexer_1 (
    .in0(buffer_1_out), .in1(buffer_2_out), .in2(AND_out), .in3(OR_out), .in4(subtractor_1_out),
    .in5(adder_1_out), .in6(subtractor_2_out), .in7(adder_2_out), .in8(not_1_out), .in9(not_2_out),
    .out(OUT), .sel(MUX_Con));  // open: in10, in11, in12, in13, in14, in15, en

  // Notes on the sheet:
  //   A - Input
  //   B - Input
  //   Output
  //   0000  - A Buffer
  //   0001 - B Buffer
  //   0010 - And (A*B)
  //   0011 -Or (A+B)
  //   0100 -Subtractor (A-B)
  //   0101 - A Increment
  //   0110 -B Decrement
  //   0111 - A+B adder
  //   1000 - A complement
  //   1001 - B complement
endmodule
