// Logisim project CPU.circ as structural Verilog: 1 circuit, main circuit main
module main (
  output [15:0] INSTRUCTION_BIN
);

  wire clock_1_out, comparator_1_gt, comparator_2_lt, main_1_jmp, main_1_load_0_str_1__immf, main_1_pwr,
       main_1_reg_write, NOT_out, OR_out;
  wire [1:0] main_1_write_source;
  wire [7:0] adder_1_out, alu_1_out, main_2_counter, main_2_out_1, main_2_out_2, multiplexer_1_out,
       multiplexer_2_out, multiplexer_3_out, not_2_out, PC_q, ram_1_data, subtractor_1_out;

  Register PC (.D(multiplexer_1_out), .en(OR_out), .Q(PC_q), .clk(clock_1_out));  // open: clr
  Multiplexer #(.width(8), .enable("false")) multiplexer_1 (
    .in0(adder_1_out), .in1(INSTRUCTION_BIN[7:0]), .out(multiplexer_1_out), .sel(main_1_jmp));
  Adder adder_1 (.a(PC_q), .b(8'h1), .out(adder_1_out));  // open: cin, cout
  or OR (OR_out, main_1_pwr, comparator_1_gt);
  ROM #(.dataWidth(16)) rom_1 (.addr(PC_q), .data(INSTRUCTION_BIN));  // open: sel
  Control_unit_main main_1 (
    .INSTRUCTION(INSTRUCTION_BIN), .REG_WRITE(main_1_reg_write), .WRITE_SOURCE(main_1_write_source),
    .JMP(main_1_jmp), .PWR(main_1_pwr), .LOAD_0_STR_1__IMMF(main_1_load_0_str_1__immf));
  Clock clock_1 (.out(clock_1_out));
  Multiplexer #(.select(2), .width(8), .enable("false")) multiplexer_2 (
    .in0(ram_1_data), .in1(alu_1_out), .in2(INSTRUCTION_BIN[7:0]), .in3(main_2_out_2),
    .out(multiplexer_2_out), .sel(main_1_write_source));
  registerbank_main main_2 (
    .DATA_IN(multiplexer_2_out), .WRITE_MODE(main_1_reg_write), .WRITE_IN_ADDRESS(INSTRUCTION_BIN[11:8]),
    .OUT_1(main_2_out_1), .OUT_2(main_2_out_2), .OUT_ADDRESS_1(INSTRUCTION_BIN[3:0]),
    .OUT_ADDRESS_2(INSTRUCTION_BIN[7:4]), .CLK(clock_1_out), .COUNTER(main_2_counter));
  Comparator #(.mode("unsigned")) comparator_1 (
    .a(main_2_counter), .b({8{1'b0}}), .gt(comparator_1_gt));  // open: eq, lt
  ALU alu_1 (.OUT(alu_1_out), .INP1(main_2_out_1), .INP2(main_2_out_2), .MUX_Con(INSTRUCTION_BIN[15:12]));
  not NOT (NOT_out, clock_1_out);
  RAM #(.addrWidth(4), .bus("separate")) ram_1 (
    .addr(INSTRUCTION_BIN[11:8]), .din(main_2_out_1), .data(ram_1_data), .str(main_1_load_0_str_1__immf),
    .clk(NOT_out));  // open: sel, ld, clr
  assign not_2_out = ~subtractor_1_out;  // NOT_Gate not_2, 8 bits wide
  Subtractor subtractor_1 (.a(ram_1_data), .b(8'h1), .out(subtractor_1_out));  // open: bin, bout
  Comparator comparator_2 (.a(ram_1_data), .b({8{1'b0}}), .lt(comparator_2_lt));  // open: gt, eq
  Multiplexer #(.width(8), .enable("false")) multiplexer_3 (
    .in0(ram_1_data), .in1(not_2_out), .out(multiplexer_3_out), .sel(comparator_2_lt));
  LED NF (.in(comparator_2_lt));
  Hex_Digit_Display hex_digit_display_1 (.value(multiplexer_3_out[3:0]));  // open: dp
  Hex_Digit_Display hex_digit_display_2 (.value(multiplexer_3_out[7:4]));  // open: dp

  // Notes on the sheet:
  //   INSTRUCTION ROM
  //   contents of rom_1 (hex, n*v repeats v):
  //   5 101 201 7312 1120 1230 b003 6000 f000 c003
  //   Counter Comparator
endmodule
