// Logisim project Control_unit.circ as structural Verilog: 1 circuit, main circuit main
module main (
  input  [15:0] INSTRUCTION,
  output [1:0] WRITE_SOURCE,
  output REG_WRITE,
  output JMP,
  output PWR,
  output LOAD_0_STR_1__IMMF
);

  wire and_1_out, and_2_out, comparator_1_eq, comparator_1_gt, comparator_1_lt, comparator_2_gt,
       comparator_2_lt;

  Comparator #(.width(4), .mode("unsigned")) comparator_1 (
    .a(INSTRUCTION[15:12]), .b(4'b0001), .gt(comparator_1_gt), .eq(comparator_1_eq), .lt(comparator_1_lt));
  Comparator #(.width(4), .mode("unsigned")) comparator_2 (
    .a(INSTRUCTION[15:12]), .b(4'b1010), .gt(comparator_2_gt), .lt(comparator_2_lt));  // open: eq
  Comparator #(.width(4), .mode("unsigned")) comparator_3 (
    .a(INSTRUCTION[15:12]), .b(4'b1100), .eq(JMP));  // open: gt, lt
  nand nand_1 (PWR, INSTRUCTION[12], INSTRUCTION[13], INSTRUCTION[14], INSTRUCTION[15]);
  and and_1 (and_1_out, INSTRUCTION[15], ~INSTRUCTION[14], INSTRUCTION[13]);  // AND_Gate
  or or_1 (WRITE_SOURCE[1], comparator_1_eq, comparator_1_lt);
  and and_2 (and_2_out, comparator_1_gt, comparator_2_lt);
  not not_1 (REG_WRITE, comparator_2_gt);
  or or_2 (WRITE_SOURCE[0], and_2_out, INSTRUCTION[12]);
  and and_3 (LOAD_0_STR_1__IMMF, and_1_out, INSTRUCTION[12]);
endmodule
